# Fritzing sketch Schematic (saved by Fritzing 0.9.3b)
breadboards: 1

parts:
  Part1 = Arduino Uno (Rev3) - ICSP
  U1 = LCD-16X2 [package=lcd-16x2]
  U2 = POT [package=pot_alpha_rv16af-20]

nets:
  N1: Part1.D8, U1.RS
  N2: Part1.D9_PWM, U1.R_W
  N3: Part1.D10_PWM/SS, U1.E
  N4: Part1.D0/RX, U1.DB0
  N5: Part1.D1/TX, U1.DB1
  N6: Part1.D2, U1.DB2
  N7: Part1.D3_PWM, U1.DB3
  N8: Part1.D4, U1.DB4
  N9: Part1.D5_PWM, U1.DB5
  N10: Part1.D6_PWM, U1.DB6
  N11: Part1.D7, U1.DB7
  5V: Part1.5V, U1.VDD, U1.A, U2.A
  GND: Part1.GND, U1.VSS, U1.K, U2.E
  N12: U1.VO, U2.S

notes:
  Rotary Potentiomer hooked to V0 controls contrast
  PORTB used for data bits 0-7 and PORTD used for data signal, read mode and clock latch
